# Fritzing sketch competicao (saved by Fritzing 0.9.3b)
breadboards: 1

parts:
  U1 = NodeMCU V1.0
  T1 = LM35 Temperature Sensor [package="TO92 [THT]"]
  Part1 = Adafruit MAX4466 Electret Microphone Amplifier [part_number="Adafruit #1063"]  # not connected
  IC1 = SELECTOR_MULTIPLEXER [package=dil16]

nets:
  N1: U1.D2, IC1.A_1A
  N2: U1.3V3, IC1.P_GND
  N3: U1.GND, IC1.A_!A!_B, IC1.A_1B, IC1.A_1Y, IC1.A_2A, IC1.A_2B
  N4: U1.A0, IC1.A_2Y
  N5: T1.Vout, IC1.A_3Y
  N6: T1.GND, IC1.A_3A, IC1.A_4Y, IC1.A_4B, IC1.A_4A, IC1.A_G, IC1.P_VCC

notes:
  Em tese eh pra funcionar sem os fios brancos, eles soh sao boas praticas

custom parts:
  NodeMCU V1.0: ESP8266 based NodeMCU
  Adafruit MAX4466 Electret Microphone Amplifier: Add an ear to your project with this well-designed electret microphone amplifier. This fully assembled and tested board comes with a 20-20KHz electret microphone soldered on. For the amplification, we use the Maxim MAX4466, an op-amp specifically designed for this delicate task! The amplifier has excellent power supply noise rejection, so this amplifier sounds really good and isn't nearly as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
